# Fritzing sketch PIR (saved by Fritzing 0.9.3b)
breadboards: 1

parts:
  Part1 = Arduino Uno (Rev3)
  VCC1 = Battery block 9V
  PIR1 = PIR sensor
  LED1 = smd LED [color="Red (633nm)" package="0603 [SMD]"]

nets:
  N1: Part1.D11_PWM/MOSI, PIR1.SIG
  N2: Part1.D13/SCK, LED1.cathode
  5V: Part1.5V, PIR1.VDD
  GND: Part1.GND, VCC1.-, PIR1.GND, LED1.anode
  N3: Part1.VIN, VCC1.+
