# Fritzing sketch Ultrasonic (saved by Fritzing 0.9.3b)
breadboards: 1

parts:
  Part1 = Arduino Uno (Rev3)
  VCC1 = Battery block 9V
  HC-SR04_Sensor_1 = HC-SR04 Ultrasonic Distance Sensor

nets:
  N1: Part1.D11_PWM/MOSI, HC-SR04_Sensor_1.TRIG
  N2: Part1.D12/MISO, HC-SR04_Sensor_1.ECHO
  5V: Part1.5V, HC-SR04_Sensor_1.VCC
  GND: Part1.GND, VCC1.-, HC-SR04_Sensor_1.GND
  N3: Part1.VIN, VCC1.+
